# Fritzing sketch percobaan_1 (saved by Fritzing 0.9.3b)
breadboards: 1

parts:
  S1 = DHT22 Sensor [package=THT]  # not connected
  U1 = ESP32S-HiLetgo [part_number=ESP32S-HiLetgo]
  DHT1 = DHT22 Humidity and Temperature Sensor
  Capacitive_Soil_Moisture_Sensor1 = Capacitive Soil Moisture Sensor V2.0

nets:
  N1: U1.3.3, DHT1.VDD
  N2: U1.EN, DHT1.GND
  N3: U1.GPIO34, Capacitive_Soil_Moisture_Sensor1.AOUT

custom parts:
  DHT22 Sensor: DHT22 Sensor (custom part - dibuat otomatis)
  ESP32S-HiLetgo: HiLetgo ESP-WROOM-32 ESP32 ESP-32S Development Board 2.4GHz Dual-Mode WiFi + Bluetooth Dual Cores Microcontroller The ESP32 integrated with Antenna switches, RF Balun, power amplifiers, low-noise amplifiers, filters, and management modules, and the entire solution occupies the least area of PCB. 2.4 GHz Wi-Fi plus Bluetooth dual-mode chip, with TSMC Ultra-low power consumption 40nm technology,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
