# Fritzing sketch percobaan_2_3 (saved by Fritzing 0.9.3b)
breadboards: 1

parts:
  S2 = DHT22 Sensor [package=THT]  # not connected
  U2 = ESP32S-HiLetgo [part_number=ESP32S-HiLetgo]
  DHT2 = DHT22 Humidity and Temperature Sensor
  Capacitive_Soil_Moisture_Sensor2 = Capacitive Soil Moisture Sensor V2.0
  R1 = Resistor [tolerance=±5% resistance=220 package="0805 [SMD]"]
  LED1 = smd LED [color="Red (633nm)" package="0603 [SMD]"]
  LED2 = smd LED [color="Yellow (592nm)" package="0603 [SMD]"]
  LED3 = smd LED [color="Green (565nm)" package="0603 [SMD]"]
  R2 = Resistor [tolerance=±5% resistance=220 package="0805 [SMD]"]
  R3 = Resistor [tolerance=±5% resistance=220 package="0805 [SMD]"]

nets:
  N1: U2.3.3, DHT2.VDD
  N2: U2.EN, DHT2.GND, LED1.cathode, LED2.cathode, LED3.cathode
  N3: U2.GPIO34, Capacitive_Soil_Moisture_Sensor2.AOUT
  N4: U2.GPIO25, R3.Pin_1
  N5: U2.GPIO26, R1.Pin_1
  N6: U2.GPIO27, R2.Pin_1
  N7: R1.Pin_0, LED2.anode
  N8: LED1.anode, R3.Pin_0
  N9: LED3.anode, R2.Pin_0

custom parts:
  DHT22 Sensor: DHT22 Sensor (custom part - dibuat otomatis)
  ESP32S-HiLetgo: HiLetgo ESP-WROOM-32 ESP32 ESP-32S Development Board 2.4GHz Dual-Mode WiFi + Bluetooth Dual Cores Microcontroller The ESP32 integrated with Antenna switches, RF Balun, power amplifiers, low-noise amplifiers, filters, and management modules, and the entire solution occupies the least area of PCB. 2.4 GHz Wi-Fi plus Bluetooth dual-mode chip, with TSMC Ultra-low power consumption 40nm technology,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
